# Fritzing sketch ArmBaseServoControl (saved by Fritzing 0.9.3b)
breadboards: 1

parts:
  Part1 = Arduino Mega 2560 (Rev3)
  J1 = Basic Servo
  S1 = Pushbutton [package="[THT]"]
  S2 = Pushbutton [package="[THT]"]
  R1 = Resistor [tolerance=±5% resistance=10k package=THT]
  R2 = Resistor [tolerance=±5% resistance=10k package=THT]

nets:
  N1: Part1.D9_PWM, J1.pulse
  5V: Part1.5V, J1.vcc, S1.Pin_1, S1.Pin_2, S2.Pin_1, S2.Pin_2
  GND: Part1.GND, J1.gnd, R1.Pin_0, R2.Pin_0
  N2: Part1.D50, S2.Pin_3, S2.Pin_4, R2.Pin_1
  N3: Part1.D52, S1.Pin_3, S1.Pin_4, R1.Pin_1

// code stored in the sketch: Arm-Base-Servo-Control-Code.ino
#include <Servo.h>

Servo armBaseServo;  

int buttonRight = 50;  
int buttonLeft = 52;

void setup() {
    armBaseServo.attach(9);
    pinMode(buttonLeft, INPUT);
    pinMode(buttonRight, INPUT);  
}

void loop() {
    int buttonLeftState = digitalRead(buttonLeft);
    int buttonRightState = digitalRead(buttonRight);
  
    if (buttonLeftState == HIGH) {
        armBaseServo.write(105);
        delay(50);
    } else if (buttonRightState == HIGH) {
        armBaseServo.write(83);
        delay(50);
    } else {
        armBaseServo.write(93);
        delay(50);
    }
}
