# Fritzing sketch UltrasonicSensorAndLCD (saved by Fritzing 0.9.3b)
breadboards: 1

parts:
  LCD1 = LCD screen
  Part1 = Arduino Mega 2560 (Rev3)
  hc-sr1 = hc-sr04
  U1 = POT [package=pot_alpha_rv16af-20]

nets:
  GND: LCD1.VSS, LCD1.R/W, LCD1.LED-, Part1.GND, hc-sr1.GND, U1.E
  VDD: LCD1.VDD, LCD1.LED+, Part1.5V, hc-sr1.VCC, U1.A
  N1: LCD1.V0, U1.S
  N2: LCD1.RS, Part1.D1_TX0
  N3: LCD1.E, Part1.D2_PWM
  N4: LCD1.DB4, Part1.D4_PWM
  N5: LCD1.DB5, Part1.D5_PWM
  N6: LCD1.DB6, Part1.D6_PWM
  N7: LCD1.DB7, Part1.D7_PWM
  N8: Part1.D10_PWM, hc-sr1.Echo
  N9: Part1.D9_PWM, hc-sr1.Trig
